# Fritzing sketch ZeitRaum-Wiring (saved by Fritzing 0.9.3b)
breadboards: 1

parts:
  Part1 = Adafruit AT42QT1010 Standalone Momentary Capacitive Touch Sensor [part_number="Adafruit #1374"]
  Part2 = Arduino Leonardo (Rev3b)
  Part3 = Adafruit AT42QT1010 Standalone Momentary Capacitive Touch Sensor [part_number="Adafruit #1374"]

nets:
  VDD: Part1.VDD, Part2.5V, Part3.VDD
  N1: Part1.OUT, Part2.D1/TX
  GND: Part1.GND, Part2.GND, Part3.GND
  N2: Part2.D0/RX, Part3.OUT

custom parts:
  Adafruit AT42QT1010 Standalone Momentary Capacitive Touch Sensor: This breakout board is the simplest way to create a project with a single "momentary" capacitive touch sensor. No microcontroller is required here - just power with 1.8 to 5.5VDC and touch the pad to activate the sensor. When a capacitive load is detected (e.g. a person touches the sensor-pad area) the red LED lights up and the output pin goes high. You can also solder a wire to the middle pad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
